// Digital circuit cpu.dig as structural Verilog
module cpu (
  input  in_1,
  input  in_2,
  input  in_3,
  input  in_4,
  input  in_5,
  input  in_6,
  input  in_7,
  input  in_8,
  input  in_9,
  input  clk,
  input  in_11,
  input  in_12
);

  wire adder_1_p10, adder_1_p11, adder_1_p12, adder_1_p13, IC_o_0, IC_o_1, IC_o_2, IC_o_3, madr_q_0,
       madr_q_1, madr_q_2, madr_q_3, memory2_1_o_0, memory2_1_o_1, memory2_1_o_2, memory2_1_o_3,
       memory2_1_o_4, memory2_1_o_5, memory2_1_o_6, memory2_1_o_7, register_simple_1_q_0,
       register_simple_1_q_1, register_simple_1_q_2, register_simple_1_q_3, register_simple_2_q_0,
       register_simple_2_q_1, register_simple_2_q_2, register_simple_2_q_3, tri_state_buffer_4bit_1_o_0,
       tri_state_buffer_4bit_1_o_1, tri_state_buffer_4bit_1_o_2, tri_state_buffer_4bit_1_o_3,
       tri_state_buffer_4bit_2_o_0, tri_state_buffer_4bit_2_o_1, tri_state_buffer_4bit_2_o_2,
       tri_state_buffer_4bit_2_o_3;

  register_simple madr (
    .E_out(in_4), .CLK(clk), .D_0(tri_state_buffer_4bit_1_o_0), .D_1(tri_state_buffer_4bit_1_o_1),
    .D_2(tri_state_buffer_4bit_1_o_2), .D_3(tri_state_buffer_4bit_1_o_3), .Q_0(madr_q_0), .Q_1(madr_q_1),
    .Q_2(madr_q_2), .Q_3(madr_q_3));
  memory2 memory2_1 (
    .a_0(madr_q_0), .a_1(madr_q_1), .a_2(madr_q_2), .a_3(madr_q_3), .E(in_3), .C(clk),
    .D_0(tri_state_buffer_4bit_1_o_0), .D_1(tri_state_buffer_4bit_1_o_1), .D_2(tri_state_buffer_4bit_1_o_2),
    .D_3(tri_state_buffer_4bit_1_o_3), .O_0(memory2_1_o_0), .O_1(memory2_1_o_1), .O_2(memory2_1_o_2),
    .O_3(memory2_1_o_3), .O_4(memory2_1_o_4), .O_5(memory2_1_o_5), .O_6(memory2_1_o_6), .O_7(memory2_1_o_7));
  tri_state_buffer_4bit tri_state_buffer_4bit_1 (
    .D_0(memory2_1_o_0), .D_1(memory2_1_o_1), .D_2(memory2_1_o_2), .D_3(memory2_1_o_3), .E(in_2),
    .O_0(tri_state_buffer_4bit_1_o_0), .O_1(tri_state_buffer_4bit_1_o_1), .O_2(tri_state_buffer_4bit_1_o_2),
    .O_3(tri_state_buffer_4bit_1_o_3));
  tri_state_buffer_4bit tri_state_buffer_4bit_2 (
    .D_0(memory2_1_o_4), .D_1(memory2_1_o_5), .D_2(memory2_1_o_6), .D_3(memory2_1_o_7), .E(in_2),
    .O_0(tri_state_buffer_4bit_2_o_0), .O_1(tri_state_buffer_4bit_2_o_1), .O_2(tri_state_buffer_4bit_2_o_2),
    .O_3(tri_state_buffer_4bit_2_o_3));
  register_simple Current_Instruction_HI (
    .E_out(in_12), .CLK(clk), .D_0(tri_state_buffer_4bit_2_o_0), .D_1(tri_state_buffer_4bit_2_o_1),
    .D_2(tri_state_buffer_4bit_2_o_2), .D_3(tri_state_buffer_4bit_2_o_3));  // open: Q_0, Q_1, Q_2, Q_3
  register_simple Current_Instruction_LO (
    .E_out(in_12), .CLK(clk), .D_0(tri_state_buffer_4bit_1_o_0), .D_1(tri_state_buffer_4bit_1_o_1),
    .D_2(tri_state_buffer_4bit_1_o_2), .D_3(tri_state_buffer_4bit_1_o_3));  // open: Q_0, Q_1, Q_2, Q_3
  tri_state_buffer_4bit tri_state_buffer_4bit_3 (
    .D_0(IC_o_0), .D_1(IC_o_1), .D_2(IC_o_2), .D_3(IC_o_3), .E(in_1), .O_0(tri_state_buffer_4bit_1_o_0),
    .O_1(tri_state_buffer_4bit_1_o_1), .O_2(tri_state_buffer_4bit_1_o_2), .O_3(tri_state_buffer_4bit_1_o_3));
  counter IC (.C(clk), .O_0(IC_o_0), .O_1(IC_o_1), .O_2(IC_o_2), .O_3(IC_o_3));
  register_simple register_simple_1 (
    .E_out(in_7), .CLK(clk), .D_0(tri_state_buffer_4bit_1_o_0), .D_1(tri_state_buffer_4bit_1_o_1),
    .D_2(tri_state_buffer_4bit_1_o_2), .D_3(tri_state_buffer_4bit_1_o_3), .Q_0(register_simple_1_q_0),
    .Q_1(register_simple_1_q_1), .Q_2(register_simple_1_q_2), .Q_3(register_simple_1_q_3));
  register_simple register_simple_2 (
    .E_out(in_8), .CLK(clk), .D_0(tri_state_buffer_4bit_1_o_0), .D_1(tri_state_buffer_4bit_1_o_1),
    .D_2(tri_state_buffer_4bit_1_o_2), .D_3(tri_state_buffer_4bit_1_o_3), .Q_0(register_simple_2_q_0),
    .Q_1(register_simple_2_q_1), .Q_2(register_simple_2_q_2), .Q_3(register_simple_2_q_3));
  tri_state_buffer_4bit tri_state_buffer_4bit_4 (
    .D_0(adder_1_p10), .D_1(adder_1_p11), .D_2(adder_1_p12), .D_3(adder_1_p13), .E(in_11),
    .O_0(tri_state_buffer_4bit_1_o_0), .O_1(tri_state_buffer_4bit_1_o_1), .O_2(tri_state_buffer_4bit_1_o_2),
    .O_3(tri_state_buffer_4bit_1_o_3));
  tri_state_buffer_4bit tri_state_buffer_4bit_5 (
    .D_0(register_simple_1_q_0), .D_1(register_simple_1_q_1), .D_2(register_simple_1_q_2),
    .D_3(register_simple_1_q_3), .E(in_5), .O_0(tri_state_buffer_4bit_1_o_0),
    .O_1(tri_state_buffer_4bit_1_o_1), .O_2(tri_state_buffer_4bit_1_o_2), .O_3(tri_state_buffer_4bit_1_o_3));
  tri_state_buffer_4bit tri_state_buffer_4bit_6 (
    .D_0(register_simple_2_q_0), .D_1(register_simple_2_q_1), .D_2(register_simple_2_q_2),
    .D_3(register_simple_2_q_3), .E(in_6), .O_0(tri_state_buffer_4bit_1_o_0),
    .O_1(tri_state_buffer_4bit_1_o_1), .O_2(tri_state_buffer_4bit_1_o_2), .O_3(tri_state_buffer_4bit_1_o_3));
  // adder adder_1: pin names not known; wires that end beside it: in_9, register_simple_1_q_0, register_simple_1_q_1, register_simple_1_q_2, register_simple_1_q_3, register_simple_2_q_0, register_simple_2_q_1, register_simple_2_q_2, register_simple_2_q_3, adder_1_p10, adder_1_p11, adder_1_p12, adder_1_p13
endmodule
